# Fritzing sketch Sch (saved by Fritzing 0.8.7b)
breadboards: 1

parts:
  U1 = attiny85 [package=dip]
  J2 = Screw terminal - 2 pins [package=THT]
  U2 = Voltage Regulator [package=to220-adj]
  R1 = Resistor [tolerance=±5% resistance=470 package=THT]
  R2 = Resistor [tolerance=±5% resistance=470 package=THT]
  J3 = Screw terminal - 2 pins [package=THT]
  J1 = Screw terminal - 2 pins [package=THT]

nets:
  N1: U1.Pin_3, J3.pin2
  N2: U1.Pin_4, U2.ADJ, R1.Pin_1, R2.Pin_1, J1.pin2
  N3: U1.Pin_5, J2.pin2, R1.Pin_0
  N4: U1.Pin_6, J2.pin1, R2.Pin_0
  N5: U1.Pin_8, U2.OUT
  N6: U2.IN, J1.pin1
