# Fritzing sketch Sch (saved by Fritzing 0.8.7b)
circuit board: 8.46667cm x 5.64444cm
perfboards: 1

parts:
  U1 = attiny85 [package=dip]
  J2 = Screw terminal - 2 pins [package=THT]
  U2 = Voltage Regulator [package=to220-adj]
  R1 = Resistor [tolerance=±5% resistance=470 package=THT]
  R2 = Resistor [tolerance=±5% resistance=470 package=THT]
  J3 = Screw terminal - 2 pins [package=THT]
  J1 = Screw terminal - 2 pins [package=THT]
  S1 = Pushbutton [package="[THT]"]
  R3 = Resistor [tolerance=±5% resistance=10k package=THT]
  LED1 = LED - 5mm [color="Red (633nm)" package="5 mm [THT]"]
  R4 = Resistor [tolerance=±5% resistance=10k package=THT]

nets:
  N1: U1.Pin_1, LED1.anode
  N2: U1.Pin_3, J3.pin1
  N3: U1.Pin_4, U2.ADJ, R1.Pin_1, R2.Pin_1, J1.pin2, R3.Pin_1, R4.Pin_1
  N4: U1.Pin_5, J2.pin2, R1.Pin_0
  N5: U1.Pin_6, J2.pin1, R2.Pin_0
  N6: U1.Pin_7, S1.Pin_3, S1.Pin_4, R3.Pin_0
  N7: U1.Pin_8, U2.OUT, S1.Pin_1, S1.Pin_2
  N8: U2.IN, J1.pin1
  N9: LED1.cathode, R4.Pin_0
